# Fritzing sketch scheme (saved by Fritzing 0.9.2b)
breadboards: 2

parts:
  Arduino = Arduino Leonardo (Rev3b)
  part = LED - 5mm [color="Red (633nm)" package="5 mm [THT]"]
  part_2 = LED - 5mm [color="Red (633nm)" package="5 mm [THT]"]
  part_3 = LED - 5mm [color="Red (633nm)" package="5 mm [THT]"]
  LED11 = RGB LED (com. cathode, rgb) [package="5 mm [THT]"]
  part_4 = LED - 5mm [color="Red (633nm)" package="5 mm [THT]"]
  part_5 = LED - 5mm [color="Red (633nm)" package="5 mm [THT]"]
  S5 = Pushbutton [package=THT]
  S6 = Pushbutton [package=THT]
  S7 = Pushbutton [package=THT]
  S4 = Pushbutton [package=THT]
  part_6 = Piezo Speaker
  part_7 = Rotary Potentiometer (Small) [maximum_resistance=100kΩ package=THT]
  part_8 = Rotary Potentiometer (Small) [maximum_resistance=100kΩ package=THT]
  S8 = Toggle Switch [package=THT]
  S9 = Toggle Switch [package=THT]
  S10 = Toggle Switch [package=THT]
  part_9 = Resistor [tolerance=±5% resistance=220 package=THT]
  part_10 = Resistor [tolerance=±5% resistance=220 package=THT]
  part_11 = Resistor [tolerance=±5% resistance=220 package=THT]
  part_12 = Resistor [tolerance=±5% resistance=220 package=THT]
  part_13 = Resistor [tolerance=±5% resistance=220 package=THT]
  part_14 = Resistor [tolerance=±5% resistance=220 package=THT]
  D1 = Rectifier Diode [part_number=1N4001 package="300 mil [THT]"]
  part_15 = LED - 5mm [color="Red (633nm)" package="5 mm [THT]"]
  part_16 = Battery block 9V

nets:
  N1: Arduino.D0/RX, S4.leg0
  N2: Arduino.D1/TX, S5.leg0
  N3: Arduino.D2/SDA, S6.leg0
  N4: Arduino.D3_PWM/SCL, part_13.Pin_1
  N5: Arduino.D4/A6, S7.leg0
  N6: Arduino.D5_PWM, part_12.Pin_1
  N7: Arduino.D6_PWM/A7, part_11.Pin_1
  N8: Arduino.D7, part_10.Pin_1
  N9: Arduino.5V, part_7.leg1, part_8.leg1
  N10: Arduino.GND, part.cathode, part_2.cathode, part_3.cathode, LED11.common_cathode, part_4.cathode, part_5.cathode, S5.leg1, S6.leg1, S7.leg1, S4.leg1, part_6.pin1, part_7.leg2, part_8.leg2, S8.COM, S9.COM, S10.COM, part_15.cathode, part_16.-
  N11: Arduino.VIN, D1.cathode
  N12: Arduino.A0, part_7.wiper
  N13: Arduino.A1, part_8.wiper
  N14: Arduino.A2, S8.L1
  N15: Arduino.A3, S9.L1
  N16: Arduino.A4, S10.L1
  N17: Arduino.D8/A8, part_6.pin2
  N18: Arduino.D9_PWM/A9, LED11.blue_anode
  N19: Arduino.D10_PWM/A10, LED11.green_anode
  N20: Arduino.D11_PWM, part_14.Pin_1
  N21: Arduino.D12/A11, part_9.Pin_1
  N22: Arduino.D13_PWM, LED11.red_anode
  N23: part.anode, part_10.Pin_0
  N24: part_2.anode, part_14.Pin_0
  N25: part_3.anode, part_9.Pin_0
  N26: part_4.anode, part_11.Pin_0
  N27: part_5.anode, part_12.Pin_0
  N28: part_13.Pin_0, part_15.anode
  N29: D1.anode, part_16.+
